# Fritzing sketch HeartbeatStationBoard_v3 (saved by Fritzing 0.9.4)
circuit board: 4.5cm x 7.8cm
breadboards: 1

parts:
  DFRobot_DFPlayer_Mini1 = DFRobot DFPlayer Mini [part_number=DFR0299]
  R1 = Resistor [tolerance=±5% resistance=10 package=THT]
  Speaker = female pin header, 3 pins [form="♀ (female)"]
  LED_0 = molex pin header, 5 pins [form=molex]
  Power = female alternating pin header, 2 pins [form="♀ (female)"]
  Vol = Trimmer Potentiometer [maximum_resistance=100kΩ package=THT]
  Arduino_Micro1 = Arduino Micro (Rev3)
  Heart_Rate = female pin header, 5 pins [form="♀ (female)"]

nets:
  VCC: DFRobot_DFPlayer_Mini1.VCC, LED_0.pin4, LED_0.pin5, Vol.leg2, Arduino_Micro1.5V
  N1: DFRobot_DFPlayer_Mini1.RX, R1.Pin_1
  N2: DFRobot_DFPlayer_Mini1.TX, Arduino_Micro1.D4_PWM/A6
  N3: DFRobot_DFPlayer_Mini1.SPK_1, Speaker.pin1
  N4: DFRobot_DFPlayer_Mini1.GND-1, DFRobot_DFPlayer_Mini1.GND-2, Speaker.pin2, LED_0.pin3, Power.pin1, Vol.leg1, Arduino_Micro1.GND, Heart_Rate.pin5
  N5: DFRobot_DFPlayer_Mini1.SPK_2, Speaker.pin3
  N6: R1.Pin_0, Arduino_Micro1.D5_PWM
  N7: LED_0.pin1, Arduino_Micro1.D3/SCL
  N8: LED_0.pin2, Arduino_Micro1.D2/SDA
  N9: Power.pin2, Arduino_Micro1.VIN
  N10: Vol.wiper, Arduino_Micro1.A4
  N11: Arduino_Micro1.D10_PWM/A10, Heart_Rate.pin1
  N12: Arduino_Micro1.D11_PWM, Heart_Rate.pin2
  N13: Arduino_Micro1.A0, Heart_Rate.pin3
  N14: Arduino_Micro1.3V3, Heart_Rate.pin4

notes:
  -
  +
